// Logisim project S1-T7.circ as structural Verilog: 2 circuits, main circuit main
module main (
  input  RESET,
  input  in_2,
  input  [3:0] in_3,
  input  in_4,
  input  [3:0] B,
  input  in_6,
  input  [3:0] in_7,
  input  in_8,
  input  [3:0] D,
  input  in_10,
  input  _0,
  input  _1,
  input  _2,
  input  [3:0] in_14,
  input  _3,
  input  _4,
  input  _5,
  input  _6,
  input  _7,
  input  _8,
  input  _9,
  input  _0_2,
  input  _0_3,
  input  _1_2,
  input  _1_3,
  input  _2_2,
  input  [3:0] in_27,
  input  _2_3,
  input  [3:0] in_29,
  input  _3_2,
  input  _3_3,
  input  _4_2,
  input  _4_3,
  input  _5_2,
  input  _5_3,
  input  _6_2,
  input  _6_3,
  input  _7_2,
  input  _7_3,
  input  _8_2,
  input  _8_3,
  input  _9_2,
  input  _9_3,
  input  _0_4,
  input  _0_5,
  input  _1_4,
  input  _1_5,
  input  _2_4,
  input  [3:0] in_49,
  input  _2_5,
  input  [3:0] in_51,
  input  _3_4,
  input  _3_5,
  input  _4_4,
  input  _4_5,
  input  _5_4,
  input  _5_5,
  input  _6_4,
  input  _6_5,
  input  _7_4,
  input  _7_5,
  input  _8_4,
  input  _8_5,
  input  _9_4,
  input  _9_5,
  input  _0_6,
  input  _0_7,
  input  _1_6,
  input  _1_7,
  input  _2_6,
  input  [3:0] in_71,
  input  _2_7,
  input  [3:0] in_73,
  input  _3_6,
  input  _3_7,
  input  _4_6,
  input  _4_7,
  input  _5_6,
  input  _5_7,
  input  _6_6,
  input  _6_7,
  input  _7_6,
  input  _7_7,
  input  _8_6,
  input  _8_7,
  input  _9_6,
  input  _9_7,
  input  _0_8,
  input  _1_8,
  input  _2_8,
  input  [3:0] in_91,
  input  _3_8,
  input  _4_8,
  input  _5_8,
  input  _6_8,
  input  _7_8,
  input  _8_8,
  input  _9_8,
  output [3:0] out_99,
  output out_100,
  output A,
  output [3:0] out_102,
  output B_2,
  output out_104,
  output [3:0] out_105,
  output C,
  output out_107,
  output D_2,
  output [3:0] out_109,
  output out_110,
  output [3:0] out_111,
  output out_112,
  output [3:0] out_113,
  output [3:0] out_114,
  output out_115,
  output [3:0] out_116,
  output [3:0] out_117,
  output [3:0] out_118,
  output [3:0] out_119,
  output [3:0] out_120
);

  wire and_1_out, and_2_out, and_3_out, and_9_out, button_1_out, button_2_out, button_3_out, button_4_out,
       button_5_out, comparator_1_eq, comparator_1_gt, comparator_1_lt, comparator_2_eq, comparator_2_gt,
       comparator_2_lt, comparator_3_eq, comparator_3_gt, comparator_3_lt, comparator_4_eq, comparator_4_gt,
       comparator_4_lt, comparator_5_eq, comparator_5_gt, comparator_5_lt, comparator_6_eq, comparator_6_gt,
       comparator_6_lt, display_1_a_2, display_1_b_2, display_1_c_2, display_1_d_2, display_1_e, display_1_f,
       display_1_g, display_2_a_2, display_2_b_2, display_2_c_2, display_2_d_2, display_2_e, display_2_f,
       display_2_g, display_3_a_2, display_3_b_2, display_3_c_2, display_3_d_2, display_3_e, display_3_f,
       display_3_g, display_4_a_2, display_4_b_2, display_4_c_2, display_4_d_2, display_4_e, display_4_f,
       display_4_g, not_1_out, not_2_out, not_3_out, not_4_out, not_5_out, not_6_out, not_7_out, not_8_out,
       not_9_out, not_10_out, not_11_out, not_12_out, not_13_out, or_1_out, or_2_out, or_3_out, or_4_out,
       or_5_out, or_6_out, or_7_out, or_8_out, or_9_out, or_10_out, or_11_out, or_12_out, or_13_out,
       or_14_out, or_15_out, or_16_out, or_17_out, or_18_out, or_19_out, or_20_out, or_21_out;
  wire [3:0] xor_1_out, xor_2_out, xor_3_out, xor_4_out, xor_5_out, xor_6_out, xor_7_out, xor_8_out;

  and and_1 (and_1_out, not_1_out, not_2_out, not_3_out, not_4_out);
  and and_2 (and_2_out, RESET, out_112);
  not not_1 (not_1_out, out_100);
  not not_2 (not_2_out, out_104);
  not not_3 (not_3_out, out_107);
  not not_4 (not_4_out, out_110);
  Register #(.width(1)) register_1 (.D(1'b1), .en(1'b1), .Q(out_100), .clk(button_2_out), .clr(button_1_out));
  Register #(.width(1)) register_2 (.D(1'b1), .en(1'b1), .Q(out_104), .clk(button_3_out), .clr(button_1_out));
  Register #(.width(1)) register_3 (.D(1'b1), .en(1'b1), .Q(out_107), .clk(button_4_out), .clr(button_1_out));
  Register #(.width(1)) register_4 (.D(1'b1), .en(1'b1), .Q(out_110), .clk(button_5_out), .clr(button_1_out));
  Button button_1 (.out(button_1_out));
  or or_1 (or_1_out, out_100, out_104, out_107, out_110);
  not not_5 (not_5_out, or_1_out);
  display display_1 (
    .A(out_99[3]), .B(out_99[2]), .C(out_99[1]), .D(out_99[0]), .a_2(display_1_a_2), .b_2(display_1_b_2),
    .c_2(display_1_c_2), .d_2(display_1_d_2), .e(display_1_e), .f(display_1_f), .g(display_1_g));
  display display_2 (
    .A(out_102[3]), .B(out_102[2]), .C(out_102[1]), .D(out_102[0]), .a_2(display_2_a_2), .b_2(display_2_b_2),
    .c_2(display_2_c_2), .d_2(display_2_d_2), .e(display_2_e), .f(display_2_f), .g(display_2_g));
  display display_3 (
    .A(out_105[3]), .B(out_105[2]), .C(out_105[1]), .D(out_105[0]), .a_2(display_3_a_2), .b_2(display_3_b_2),
    .c_2(display_3_c_2), .d_2(display_3_d_2), .e(display_3_e), .f(display_3_f), .g(display_3_g));
  display display_4 (
    .A(out_109[3]), .B(out_109[2]), .C(out_109[1]), .D(out_109[0]), .a_2(display_4_a_2), .b_2(display_4_b_2),
    .c_2(display_4_c_2), .d_2(display_4_d_2), .e(display_4_e), .f(display_4_f), .g(display_4_g));
  _7_Segment_Display u_7_segment_display_1 (
    .g(display_1_g), .f(display_1_f), .a(display_1_a_2), .b(display_1_b_2), .e(display_1_e),
    .d(display_1_d_2), .c(display_1_c_2));  // open: dp
  _7_Segment_Display u_7_segment_display_2 (
    .g(display_2_g), .f(display_2_f), .a(display_2_a_2), .b(display_2_b_2), .e(display_2_e),
    .d(display_2_d_2), .c(display_2_c_2));  // open: dp
  _7_Segment_Display u_7_segment_display_3 (
    .g(display_3_g), .f(display_3_f), .a(display_3_a_2), .b(display_3_b_2), .e(display_3_e),
    .d(display_3_d_2), .c(display_3_c_2));  // open: dp
  _7_Segment_Display u_7_segment_display_4 (
    .g(display_4_g), .f(display_4_f), .a(display_4_a_2), .b(display_4_b_2), .e(display_4_e),
    .d(display_4_d_2), .c(display_4_c_2));  // open: dp
  and and_3 (and_3_out, and_1_out, out_115);
  Button button_2 (.out(button_2_out));
  Button button_3 (.out(button_3_out));
  Button button_4 (.out(button_4_out));
  Button button_5 (.out(button_5_out));
  Priority_Encoder #(.select(4)) priority_encoder_1 (
    .in0(_0_2), .in1(_1_2), .in2(_2_2), .in3(_3_2), .in4(_4_2), .in5(_5_2), .in6(_6_2), .in7(_7_2),
    .in8(_8_2), .in9(_9_2), .out(out_113), .en_in(not_5_out));  // open: in10, in11, in12, in13, in14, in15, gs, en_out
  Priority_Encoder #(.select(4)) priority_encoder_2 (
    .in0(_0_4), .in1(_1_4), .in2(_2_4), .in3(_3_4), .in4(_4_4), .in5(_5_4), .in6(_6_4), .in7(_7_4),
    .in8(_8_4), .in9(_9_4), .out(out_116), .en_in(not_5_out));  // open: in10, in11, in12, in13, in14, in15, gs, en_out
  Priority_Encoder #(.select(4)) priority_encoder_3 (
    .in0(_0_6), .in1(_1_6), .in2(_2_6), .in3(_3_6), .in4(_4_6), .in5(_5_6), .in6(_6_6), .in7(_7_6),
    .in8(_8_6), .in9(_9_6), .out(out_118), .en_in(not_5_out));  // open: in10, in11, in12, in13, in14, in15, gs, en_out
  Priority_Encoder #(.select(4)) priority_encoder_4 (
    .in0(_0_8), .in1(_1_8), .in2(_2_8), .in3(_3_8), .in4(_4_8), .in5(_5_8), .in6(_6_8), .in7(_7_8),
    .in8(_8_8), .in9(_9_8), .out(out_120), .en_in(not_5_out));  // open: in10, in11, in12, in13, in14, in15, gs, en_out
  Counter #(.width(4), .max('hf)) counter_1 (
    .load(in_2), .D(in_3), .count(and_3_out), .Q(out_99), .clk(button_2_out), .clr(and_2_out));  // open: carry
  Counter #(.width(4), .max('hf)) counter_2 (
    .load(in_4), .D(B), .count(and_3_out), .Q(out_102), .clk(button_3_out), .clr(and_2_out));  // open: carry
  Counter #(.width(4), .max('hf)) counter_3 (
    .load(in_6), .D(in_7), .count(and_3_out), .Q(out_105), .clk(button_4_out), .clr(and_2_out));  // open: carry
  Counter #(.width(4), .max('hf)) counter_4 (
    .load(in_8), .D(D), .count(and_3_out), .Q(out_109), .clk(button_5_out), .clr(and_2_out));  // open: carry
  assign xor_1_out = in_27 ^ out_113;  // XOR_Gate xor_1, 4 bits wide
  assign xor_2_out = in_49 ^ out_116;  // XOR_Gate xor_2, 4 bits wide
  assign xor_3_out = in_71 ^ out_118;  // XOR_Gate xor_3, 4 bits wide
  assign xor_4_out = in_91 ^ out_120;  // XOR_Gate xor_4, 4 bits wide
  Comparator #(.width(4), .mode("unsigned")) comparator_1 (
    .a(out_99), .b(out_102), .gt(comparator_1_gt), .eq(comparator_1_eq), .lt(comparator_1_lt));
  Comparator #(.width(4), .mode("unsigned")) comparator_2 (
    .a(out_102), .b(out_105), .gt(comparator_2_gt), .eq(comparator_2_eq), .lt(comparator_2_lt));
  Comparator #(.width(4), .mode("unsigned")) comparator_3 (
    .a(out_105), .b(out_109), .gt(comparator_3_gt), .eq(comparator_3_eq), .lt(comparator_3_lt));
  Comparator #(.width(4), .mode("unsigned")) comparator_4 (
    .a(out_99), .b(out_109), .gt(comparator_4_gt), .eq(comparator_4_eq), .lt(comparator_4_lt));
  Comparator #(.width(4), .mode("unsigned")) comparator_5 (
    .a(out_102), .b(out_109), .gt(comparator_5_gt), .eq(comparator_5_eq), .lt(comparator_5_lt));
  Comparator #(.width(4), .mode("unsigned")) comparator_6 (
    .a(out_99), .b(out_105), .gt(comparator_6_gt), .eq(comparator_6_eq), .lt(comparator_6_lt));
  or or_2 (or_2_out, xor_1_out[0], xor_1_out[1], xor_1_out[2], xor_1_out[3]);
  or or_3 (or_3_out, xor_2_out[0], xor_2_out[1], xor_2_out[2], xor_2_out[3]);
  or or_4 (or_4_out, xor_3_out[0], xor_3_out[1], xor_3_out[2], xor_3_out[3]);
  or or_5 (or_5_out, xor_4_out[0], xor_4_out[1], xor_4_out[2], xor_4_out[3]);
  or or_6 (or_6_out, comparator_1_gt, comparator_1_eq);
  or or_7 (or_7_out, comparator_1_eq, comparator_1_lt);
  or or_8 (or_8_out, comparator_2_gt, comparator_2_eq);
  or or_9 (or_9_out, comparator_2_eq, comparator_2_lt);
  or or_10 (or_10_out, comparator_3_gt, comparator_3_eq);
  or or_11 (or_11_out, comparator_3_eq, comparator_3_lt);
  or or_12 (or_12_out, comparator_4_gt, comparator_4_eq);
  or or_13 (or_13_out, comparator_4_eq, comparator_4_lt);
  or or_14 (or_14_out, comparator_5_gt, comparator_5_eq);
  or or_15 (or_15_out, comparator_5_eq, comparator_5_lt);
  or or_16 (or_16_out, comparator_6_gt, comparator_6_eq);
  or or_17 (or_17_out, comparator_6_eq, comparator_6_lt);
  not not_6 (not_6_out, or_2_out);
  not not_7 (not_7_out, or_3_out);
  not not_8 (not_8_out, or_4_out);
  not not_9 (not_9_out, or_5_out);
  and and_4 (out_115, not_6_out, not_7_out, not_8_out, not_9_out);
  and and_5 (A, or_6_out, or_16_out, or_12_out, and_9_out);
  and and_6 (B_2, or_7_out, or_8_out, or_14_out, and_9_out);
  and and_7 (C, or_9_out, or_10_out, or_17_out, and_9_out);
  and and_8 (D_2, or_11_out, and_9_out, or_13_out, or_15_out);
  LED led_1 (.in(out_115));
  and and_9 (and_9_out, in_10, out_112);
  Priority_Encoder #(.select(4)) priority_encoder_5 (
    .in0(_0), .in1(_1), .in2(_2), .in3(_3), .in4(_4), .in5(_5), .in6(_6), .in7(_7), .in8(_8), .in9(_9),
    .out(out_111));  // open: in10, in11, in12, in13, in14, in15, gs, en_out, en_in
  Priority_Encoder #(.select(4)) priority_encoder_6 (
    .in0(_0_3), .in1(_1_3), .in2(_2_3), .in3(_3_3), .in4(_4_3), .in5(_5_3), .in6(_6_3), .in7(_7_3),
    .in8(_8_3), .in9(_9_3), .out(out_114));  // open: in10, in11, in12, in13, in14, in15, gs, en_out, en_in
  Priority_Encoder #(.select(4)) priority_encoder_7 (
    .in0(_0_5), .in1(_1_5), .in2(_2_5), .in3(_3_5), .in4(_4_5), .in5(_5_5), .in6(_6_5), .in7(_7_5),
    .in8(_8_5), .in9(_9_5), .out(out_117));  // open: in10, in11, in12, in13, in14, in15, gs, en_out, en_in
  Priority_Encoder #(.select(4)) priority_encoder_8 (
    .in0(_0_7), .in1(_1_7), .in2(_2_7), .in3(_3_7), .in4(_4_7), .in5(_5_7), .in6(_6_7), .in7(_7_7),
    .in8(_8_7), .in9(_9_7), .out(out_119));  // open: in10, in11, in12, in13, in14, in15, gs, en_out, en_in
  assign xor_5_out = in_14 ^ out_111;  // XOR_Gate xor_5, 4 bits wide
  assign xor_6_out = in_29 ^ out_114;  // XOR_Gate xor_6, 4 bits wide
  assign xor_7_out = in_51 ^ out_117;  // XOR_Gate xor_7, 4 bits wide
  assign xor_8_out = in_73 ^ out_119;  // XOR_Gate xor_8, 4 bits wide
  or or_18 (or_18_out, xor_7_out[0], xor_7_out[1], xor_7_out[2], xor_7_out[3]);
  or or_19 (or_19_out, xor_8_out[0], xor_8_out[1], xor_8_out[2], xor_8_out[3]);
  or or_20 (or_20_out, xor_5_out[0], xor_5_out[1], xor_5_out[2], xor_5_out[3]);
  or or_21 (or_21_out, xor_6_out[0], xor_6_out[1], xor_6_out[2], xor_6_out[3]);
  not not_10 (not_10_out, or_18_out);
  not not_11 (not_11_out, or_19_out);
  not not_12 (not_12_out, or_20_out);
  not not_13 (not_13_out, or_21_out);
  and and_10 (out_112, not_12_out, not_13_out, not_10_out, not_11_out);
  LED led_2 (.in(out_112));

  // Notes on the sheet:
  //   TEAM MEMBERS
  //   GNANA JYOTHI, 221CS118
  //   P. HASITHA, 221CS139
  //   STHUTHI S, 221CS156
  //   PRESS TO ENTER 
  //   PASSWORD
  //   VOTING COUNTER
  //   CAST YOUR VOTE HERE
  //   A
  //   C
  //   ENTER YOUR PASSWORD HERE
  //   SECURE VOTE
  //   A B
  //   B C
  //   C D
  //   BD
  //   AC
  //   U
  //   V
  //   W
  //   A D
  //   X
  //   Y
  //   Z
  //   GREEN-PASSWORD MATCH
  //   RED-PASSWORD MISMATCH
  //   WINNER
  //   DISPLAY
  //   GREEN-PASSWORD MATCH
  //   RED-PASSWORD MISMATCH
endmodule

module display (
  input  A,
  input  B,
  input  C,
  input  D,
  output a_2,
  output b_2,
  output c_2,
  output d_2,
  output e,
  output f,
  output g
);

  wire and_1_out, and_2_out, and_3_out, and_4_out, and_5_out, and_6_out, and_7_out, and_8_out, and_9_out,
       and_10_out, and_11_out, and_12_out, and_13_out, and_14_out, and_15_out, and_16_out, not_1_out,
       not_2_out, not_3_out, not_4_out, not_5_out, not_6_out, not_7_out, not_8_out, not_9_out, not_10_out,
       not_11_out, not_12_out, not_13_out, not_14_out, not_15_out, not_16_out, not_17_out, not_18_out,
       not_19_out, not_20_out, not_21_out;

  not not_1 (not_1_out, B);
  not not_2 (not_2_out, D);
  not not_3 (not_3_out, C);
  not not_4 (not_4_out, D);
  not not_5 (not_5_out, C);
  not not_6 (not_6_out, B);
  not not_7 (not_7_out, D);
  not not_8 (not_8_out, B);
  not not_9 (not_9_out, D);
  not not_10 (not_10_out, C);
  not not_11 (not_11_out, B);
  not not_12 (not_12_out, D);
  not not_13 (not_13_out, D);
  not not_14 (not_14_out, C);
  not not_15 (not_15_out, D);
  not not_16 (not_16_out, C);
  not not_17 (not_17_out, D);
  not not_18 (not_18_out, B);
  not not_19 (not_19_out, C);
  not not_20 (not_20_out, D);
  and and_1 (and_1_out, not_1_out, not_2_out);
  and and_2 (and_2_out, B, D);
  not not_21 (not_21_out, B);
  and and_3 (and_3_out, not_3_out, not_4_out);
  and and_4 (and_4_out, C, D);
  or or_1 (c_2, not_5_out, D, B);
  and and_5 (and_5_out, not_6_out, not_7_out);
  and and_6 (and_6_out, not_8_out, C);
  and and_7 (and_7_out, C, not_9_out);
  and and_8 (and_8_out, B, not_10_out, D);
  and and_9 (and_9_out, not_11_out, not_12_out);
  and and_10 (and_10_out, C, not_13_out);
  and and_11 (and_11_out, not_14_out, not_15_out);
  and and_12 (and_12_out, B, not_16_out);
  and and_13 (and_13_out, B, not_17_out);
  and and_14 (and_14_out, not_18_out, C);
  and and_15 (and_15_out, B, not_19_out);
  and and_16 (and_16_out, B, not_20_out);
  or or_2 (a_2, and_1_out, C, and_2_out, A);
  or or_3 (b_2, not_21_out, and_3_out, and_4_out);
  or or_4 (d_2, and_5_out, and_6_out, and_7_out, and_8_out, A);
  or or_5 (e, and_9_out, and_10_out);
  or or_6 (f, and_11_out, and_12_out, and_13_out, A);
  or or_7 (g, and_14_out, and_15_out, and_16_out, A);

  // Notes on the sheet:
  //   7-SEGMENT DISPLAY
endmodule
